# Fritzing sketch arduino-ponggame (saved by Fritzing 0.9.3b)
breadboards: 1

parts:
  부품1 = Arduino Nano (Rev3.0)
  Grove1 = Grove OLED 128x96
  RE1 = Rotary Encoder [package=THT]
  RE2 = Rotary Encoder [package=THT]
  J1 = Piezo Speaker

nets:
  GND: 부품1.GND, Grove1.GND, RE1.EncoderPinB, RE2.EncoderPinB, J1.pin1
  5V: 부품1.5V, Grove1.VCC, RE1.EncoderPinA, RE2.EncoderPinA
  N1: 부품1.A5, Grove1.SCL
  N2: 부품1.A4, Grove1.SDA
  N3: 부품1.A1, RE1.EncoderPinC
  N4: 부품1.A0, RE2.EncoderPinC
